# Fritzing sketch arduino-reset-block (saved by Fritzing 0.9.6b)

parts:
  Part1 = Arduino Uno (Rev3) - ICSP
  Capacitor = Ceramic Capacitor [capacitance=10µF voltage=6.3V package="200 mil [THT, multilayer]"]

nets:
  N1: Part1.RESET, Capacitor.1
  N2: Part1.GND, Capacitor.0
